// Logisim project ex1_try.circ as structural Verilog: 1 circuit, main circuit main
module main (
  input  in_1,
  input  in_2,
  input  in_3,
  input  in_4,
  input  in_5,
  input  in_6,
  input  [1:0] in_7,
  input  in_8,
  input  [1:0] in_9,
  input  in_10,
  output out_11,
  output out_12,
  output out_13,
  output out_14,
  output out_15,
  output out_16,
  output [1:0] out_17
);

  and and_1 (out_11, in_2, in_1);
  Multiplexer multiplexer_1 (.in0(in_7[0]), .in1(in_9[0]), .out(out_17[0]), .sel(in_9[0]));
  // Pins of 1 and 2 bits meet at in_7
  // Pins of 1 and 2 bits meet at in_9
  // Pins of 1 and 2 bits meet at out_17

  assign in_6 = in_4;
  assign in_10 = in_9[0];
  assign out_12 = out_11;
  assign out_13 = in_3;
  assign out_14 = in_4;
  assign out_15 = in_5;

  // Notes on the sheet:
  //   we are indentical!
  //   different colours
endmodule
